// Logisim project trabalho_logica.circ as structural Verilog: 21 circuits, main circuit ULA
module ULA (
  input  [3:0] AluOP,
  input  [31:0] A,
  input  [31:0] B,
  output tudo_zer_cont,
  output [31:0] RESULTED,
  output tudo_zer_logic
);

  wire [31:0] blobo_cont_1_resulted, bloco_logico_1_resulted;

  BLOBO_CONT blobo_cont_1 (.AluOp(AluOP), .A(A), .B(B), .RESULTED(blobo_cont_1_resulted), .tudo_zero(tudo_zer_cont));
  BLOCO_LOGICO bloco_logico_1 (
    .S1_S2_S3(AluOP), .A(A), .B(B), .RESULTED(bloco_logico_1_resulted), .tudo_zero(tudo_zer_logic));
  assign RESULTED = blobo_cont_1_resulted | bloco_logico_1_resulted;  // OR_Gate or_1, 32 bits wide
endmodule

module comparador (
  input  [31:0] A,
  input  [31:0] B,
  input  [31:0] C,
  input  [31:0] D,
  output tudo_zero
);

  wire not_1_out, not_2_out, not_3_out, not_4_out, or_1_out, or_2_out, or_3_out, or_4_out;

  or or_1 (or_1_out, A[31], A[30], A[29], A[28], A[27], A[26], A[25], A[24], A[23], A[22], A[21], A[20], A[19], A[18], A[17], A[16], A[15], A[14], A[13], A[12], A[11], A[10], A[9], A[8], A[7], A[6], A[5], A[4], A[3], A[2], A[1], A[0]);
  or or_2 (or_2_out, B[31], B[30], B[29], B[28], B[27], B[26], B[25], B[24], B[23], B[22], B[21], B[20], B[19], B[18], B[17], B[16], B[15], B[14], B[13], B[12], B[11], B[10], B[9], B[8], B[7], B[6], B[5], B[4], B[3], B[2], B[1], B[0]);
  or or_3 (or_3_out, C[31], C[30], C[29], C[28], C[27], C[26], C[25], C[24], C[23], C[22], C[21], C[20], C[19], C[18], C[17], C[16], C[15], C[14], C[13], C[12], C[11], C[10], C[9], C[8], C[7], C[6], C[5], C[4], C[3], C[2], C[1], C[0]);
  or or_4 (or_4_out, D[31], D[30], D[29], D[28], D[27], D[26], D[25], D[24], D[23], D[22], D[21], D[20], D[19], D[18], D[17], D[16], D[15], D[14], D[13], D[12], D[11], D[10], D[9], D[8], D[7], D[6], D[5], D[4], D[3], D[2], D[1], D[0]);
  not not_1 (not_1_out, or_2_out);
  not not_2 (not_2_out, or_3_out);
  not not_3 (not_3_out, or_1_out);
  not not_4 (not_4_out, or_4_out);
  and and_1 (tudo_zero, not_3_out, not_1_out, not_2_out, not_4_out);
endmodule

module halfadder (
  input  a,
  input  b,
  output S,
  output Co
);

  xor xor_1 (S, a, b);
  and and_1 (Co, a, b);
endmodule

module fulladder (
  input  ci,
  input  a,
  input  b,
  output S,
  output Co
);

  wire halfadder_1_co, halfadder_1_s, halfadder_2_co;

  halfadder halfadder_1 (.a(a), .b(b), .S(halfadder_1_s), .Co(halfadder_1_co));
  halfadder halfadder_2 (.a(ci), .b(halfadder_1_s), .S(S), .Co(halfadder_2_co));
  or or_1 (Co, halfadder_2_co, halfadder_1_co);
endmodule

module add_sub_32bits (
  input  Ci,
  input  A0,
  input  B0,
  input  A1,
  input  B1,
  input  A2,
  input  B2,
  input  A3,
  input  B3,
  input  A4,
  input  B4,
  input  A5,
  input  B5,
  input  A6,
  input  B6,
  input  A7,
  input  B7,
  input  A8,
  input  B8,
  input  A9,
  input  B9,
  input  A10,
  input  B10,
  input  A11,
  input  B11,
  input  A12,
  input  B12,
  input  A13,
  input  B13,
  input  A14,
  input  B14,
  input  A15,
  input  B15,
  input  A16,
  input  B16,
  input  A17,
  input  B17,
  input  A18,
  input  B18,
  input  A19,
  input  B19,
  input  A20,
  input  B20,
  input  A21,
  input  B21,
  input  A22,
  input  B22,
  input  A23,
  input  B23,
  input  A24,
  input  B24,
  input  A25,
  input  B25,
  input  A26,
  input  B26,
  input  A27,
  input  B27,
  input  A28,
  input  B28,
  input  A29,
  input  B29,
  input  A30,
  input  B30,
  input  A31,
  input  B31,
  output S0,
  output S1,
  output S2,
  output S3,
  output S4,
  output S5,
  output S6,
  output S7,
  output S8,
  output S9,
  output S10,
  output S11,
  output S12,
  output S13,
  output S14,
  output S15,
  output S16,
  output S17,
  output S18,
  output S19,
  output S20,
  output S21,
  output S22,
  output S23,
  output S24,
  output S25,
  output S26,
  output S27,
  output S28,
  output S29,
  output S30,
  output S31,
  output OVERFLOW
);

  wire fulladder_1_co, fulladder_2_co, fulladder_3_co, fulladder_4_co, fulladder_5_co, fulladder_6_co,
       fulladder_7_co, fulladder_8_co, fulladder_9_co, fulladder_10_co, fulladder_11_co, fulladder_12_co,
       fulladder_13_co, fulladder_14_co, fulladder_15_co, fulladder_16_co, fulladder_17_co, fulladder_18_co,
       fulladder_19_co, fulladder_20_co, fulladder_21_co, fulladder_22_co, fulladder_23_co, fulladder_24_co,
       fulladder_25_co, fulladder_26_co, fulladder_27_co, fulladder_28_co, fulladder_29_co, fulladder_30_co,
       fulladder_31_co, fulladder_32_co, xor_1_out, xor_2_out, xor_3_out, xor_4_out, xor_5_out, xor_6_out,
       xor_7_out, xor_8_out, xor_9_out, xor_10_out, xor_11_out, xor_12_out, xor_13_out, xor_14_out,
       xor_15_out, xor_16_out, xor_17_out, xor_18_out, xor_19_out, xor_20_out, xor_21_out, xor_22_out,
       xor_23_out, xor_24_out, xor_25_out, xor_26_out, xor_27_out, xor_28_out, xor_29_out, xor_30_out,
       xor_31_out, xor_32_out;

  xor xor_1 (xor_1_out, B0, Ci);
  xor xor_2 (xor_2_out, B1, Ci);
  xor xor_3 (xor_3_out, B2, Ci);
  xor xor_4 (xor_4_out, B3, Ci);
  xor xor_5 (xor_5_out, B4, Ci);
  xor xor_6 (xor_6_out, B5, Ci);
  xor xor_7 (xor_7_out, B6, Ci);
  xor xor_8 (xor_8_out, B7, Ci);
  xor xor_9 (xor_9_out, B8, Ci);
  xor xor_10 (xor_10_out, B9, Ci);
  xor xor_11 (xor_11_out, B10, Ci);
  xor xor_12 (xor_12_out, B11, Ci);
  xor xor_13 (xor_13_out, B12, Ci);
  xor xor_14 (xor_14_out, B13, Ci);
  xor xor_15 (xor_15_out, B14, Ci);
  xor xor_16 (xor_16_out, B15, Ci);
  xor xor_17 (xor_17_out, B16, Ci);
  xor xor_18 (xor_18_out, B17, Ci);
  xor xor_19 (xor_19_out, B18, Ci);
  xor xor_20 (xor_20_out, B19, Ci);
  xor xor_21 (xor_21_out, B20, Ci);
  xor xor_22 (xor_22_out, B21, Ci);
  xor xor_23 (xor_23_out, B22, Ci);
  xor xor_24 (xor_24_out, B23, Ci);
  xor xor_25 (xor_25_out, B24, Ci);
  xor xor_26 (xor_26_out, B25, Ci);
  xor xor_27 (xor_27_out, B26, Ci);
  xor xor_28 (xor_28_out, B27, Ci);
  xor xor_29 (xor_29_out, B28, Ci);
  xor xor_30 (xor_30_out, B29, Ci);
  xor xor_31 (xor_31_out, B30, Ci);
  xor xor_32 (xor_32_out, B31, Ci);
  fulladder fulladder_1 (.ci(Ci), .a(A0), .b(xor_1_out), .S(S0), .Co(fulladder_1_co));
  fulladder fulladder_2 (.ci(fulladder_1_co), .a(A1), .b(xor_2_out), .S(S1), .Co(fulladder_2_co));
  fulladder fulladder_3 (.ci(fulladder_2_co), .a(A2), .b(xor_3_out), .S(S2), .Co(fulladder_3_co));
  fulladder fulladder_4 (.ci(fulladder_3_co), .a(A3), .b(xor_4_out), .S(S3), .Co(fulladder_4_co));
  fulladder fulladder_5 (.ci(fulladder_4_co), .a(A4), .b(xor_5_out), .S(S4), .Co(fulladder_5_co));
  fulladder fulladder_6 (.ci(fulladder_5_co), .a(A5), .b(xor_6_out), .S(S5), .Co(fulladder_6_co));
  fulladder fulladder_7 (.ci(fulladder_6_co), .a(A6), .b(xor_7_out), .S(S6), .Co(fulladder_7_co));
  fulladder fulladder_8 (.ci(fulladder_7_co), .a(A7), .b(xor_8_out), .S(S7), .Co(fulladder_8_co));
  fulladder fulladder_9 (.ci(fulladder_8_co), .a(A8), .b(xor_9_out), .S(S8), .Co(fulladder_9_co));
  fulladder fulladder_10 (.ci(fulladder_9_co), .a(A9), .b(xor_10_out), .S(S9), .Co(fulladder_10_co));
  fulladder fulladder_11 (.ci(fulladder_10_co), .a(A10), .b(xor_11_out), .S(S10), .Co(fulladder_11_co));
  fulladder fulladder_12 (.ci(fulladder_11_co), .a(A11), .b(xor_12_out), .S(S11), .Co(fulladder_12_co));
  fulladder fulladder_13 (.ci(fulladder_12_co), .a(A12), .b(xor_13_out), .S(S12), .Co(fulladder_13_co));
  fulladder fulladder_14 (.ci(fulladder_13_co), .a(A13), .b(xor_14_out), .S(S13), .Co(fulladder_14_co));
  fulladder fulladder_15 (.ci(fulladder_14_co), .a(A14), .b(xor_15_out), .S(S14), .Co(fulladder_15_co));
  fulladder fulladder_16 (.ci(fulladder_15_co), .a(A15), .b(xor_16_out), .S(S15), .Co(fulladder_16_co));
  fulladder fulladder_17 (.ci(fulladder_16_co), .a(A16), .b(xor_17_out), .S(S16), .Co(fulladder_17_co));
  fulladder fulladder_18 (.ci(fulladder_17_co), .a(A17), .b(xor_18_out), .S(S17), .Co(fulladder_18_co));
  fulladder fulladder_19 (.ci(fulladder_18_co), .a(A18), .b(xor_19_out), .S(S18), .Co(fulladder_19_co));
  fulladder fulladder_20 (.ci(fulladder_19_co), .a(A19), .b(xor_20_out), .S(S19), .Co(fulladder_20_co));
  fulladder fulladder_21 (.ci(fulladder_20_co), .a(A20), .b(xor_21_out), .S(S20), .Co(fulladder_21_co));
  fulladder fulladder_22 (.ci(fulladder_21_co), .a(A21), .b(xor_22_out), .S(S21), .Co(fulladder_22_co));
  fulladder fulladder_23 (.ci(fulladder_22_co), .a(A22), .b(xor_23_out), .S(S22), .Co(fulladder_23_co));
  fulladder fulladder_24 (.ci(fulladder_23_co), .a(A23), .b(xor_24_out), .S(S23), .Co(fulladder_24_co));
  fulladder fulladder_25 (.ci(fulladder_24_co), .a(A24), .b(xor_25_out), .S(S24), .Co(fulladder_25_co));
  fulladder fulladder_26 (.ci(fulladder_25_co), .a(A25), .b(xor_26_out), .S(S25), .Co(fulladder_26_co));
  fulladder fulladder_27 (.ci(fulladder_26_co), .a(A26), .b(xor_27_out), .S(S26), .Co(fulladder_27_co));
  fulladder fulladder_28 (.ci(fulladder_27_co), .a(A27), .b(xor_28_out), .S(S27), .Co(fulladder_28_co));
  fulladder fulladder_29 (.ci(fulladder_28_co), .a(A28), .b(xor_29_out), .S(S28), .Co(fulladder_29_co));
  fulladder fulladder_30 (.ci(fulladder_29_co), .a(A29), .b(xor_30_out), .S(S29), .Co(fulladder_30_co));
  fulladder fulladder_31 (.ci(fulladder_30_co), .a(A30), .b(xor_31_out), .S(S30), .Co(fulladder_31_co));
  fulladder fulladder_32 (.ci(fulladder_31_co), .a(A31), .b(xor_32_out), .S(S31), .Co(fulladder_32_co));
  xor xor_33 (OVERFLOW, fulladder_32_co, Ci);
endmodule

module overflow (
  input  Ci,
  input  A,
  input  B,
  output out_4,
  output out_5,
  output out_6
);

  wire halfadder_1_co, halfadder_1_s, halfadder_2_co;

  halfadder halfadder_1 (.a(A), .b(B), .S(halfadder_1_s), .Co(halfadder_1_co));
  halfadder halfadder_2 (.a(Ci), .b(halfadder_1_s), .S(out_4), .Co(halfadder_2_co));
  or or_1 (out_5, halfadder_2_co, halfadder_1_co);
  xor xor_1 (out_6, out_5, Ci);
endmodule

module stl (
  input  [31:0] A,
  input  [31:0] B,
  output [31:0] out_3
);

  wire not_1_out;
  wire [31:0] sub_resumido_32bits_1_out_3;

  sub_resumido_32bits sub_resumido_32bits_1 (.A(A), .B(B), .out_3(sub_resumido_32bits_1_out_3));
  not not_1 (not_1_out, sub_resumido_32bits_1_out_3[31]);
  xor xor_1 (out_3[31], 1'b1, not_1_out);

  assign out_3[30:0] = {31{out_3[31]}};

  // Notes on the sheet:
  //   constant = 1
endmodule

module add_sub_resumido_32bits (
  input  [31:0] A,
  input  CONST,
  input  [31:0] B,
  output [31:0] out_4
);

  wire add_sub_32bits_1_overflow;

  add_sub_32bits add_sub_32bits_1 (
    .Ci(CONST), .A0(A[0]), .B0(B[0]), .A1(A[1]), .B1(B[1]), .A2(A[2]), .B2(B[2]), .A3(A[3]), .B3(B[3]),
    .A4(A[4]), .B4(B[4]), .A5(A[5]), .B5(B[5]), .A6(A[6]), .B6(B[6]), .A7(A[7]), .B7(B[7]), .A8(A[8]),
    .B8(B[8]), .A9(A[9]), .B9(B[9]), .A10(A[10]), .B10(B[10]), .A11(A[11]), .B11(B[11]), .A12(A[12]),
    .B12(B[12]), .A13(A[13]), .B13(B[13]), .A14(A[14]), .B14(B[14]), .A15(A[15]), .B15(B[15]), .A16(A[16]),
    .B16(B[16]), .A17(A[17]), .B17(B[17]), .A18(A[18]), .B18(B[18]), .A19(A[19]), .B19(B[19]), .A20(A[20]),
    .B20(B[20]), .A21(A[21]), .B21(B[21]), .A22(A[22]), .B22(B[22]), .A23(A[23]), .B23(B[23]), .A24(A[24]),
    .B24(B[24]), .A25(A[25]), .B25(B[25]), .A26(A[26]), .B26(B[26]), .A27(A[27]), .B27(B[27]), .A28(A[28]),
    .B28(B[28]), .A29(A[29]), .B29(B[29]), .A30(A[30]), .B30(B[30]), .A31(A[31]), .B31(B[31]), .S0(out_4[0]),
    .S1(out_4[1]), .S2(out_4[2]), .S3(out_4[3]), .S4(out_4[4]), .S5(out_4[5]), .S6(out_4[6]), .S7(out_4[7]),
    .S8(out_4[8]), .S9(out_4[9]), .S10(out_4[10]), .S11(out_4[11]), .S12(out_4[12]), .S13(out_4[13]),
    .S14(out_4[14]), .S15(out_4[15]), .S16(out_4[16]), .S17(out_4[17]), .S18(out_4[18]), .S19(out_4[19]),
    .S20(out_4[20]), .S21(out_4[21]), .S22(out_4[22]), .S23(out_4[23]), .S24(out_4[24]), .S25(out_4[25]),
    .S26(out_4[26]), .S27(out_4[27]), .S28(out_4[28]), .S29(out_4[29]), .S30(out_4[30]), .S31(out_4[31]),
    .OVERFLOW(add_sub_32bits_1_overflow));
  LED led_1 (.in(add_sub_32bits_1_overflow));

  // Notes on the sheet:
  //   constante = 0
endmodule

module sub_resumido_32bits (
  input  [31:0] A,
  input  [31:0] B,
  output [31:0] out_3
);

  add_sub_resumido_32bits add_sub_resumido_32bits_1 (.A(A), .CONST(1'b1), .B(B), .out_4(out_3));
endmodule

module add_resumido_32bits (
  input  [31:0] A,
  input  [31:0] B,
  output [31:0] out_3
);

  add_sub_resumido_32bits add_sub_resumido_32bits_1 (.A(A), .CONST(1'b0), .B(B), .out_4(out_3));
endmodule

module MUX_2_1_32bit (
  input  S,
  input  A0,
  input  A1,
  input  A2,
  input  A3,
  input  A4,
  input  A5,
  input  A6,
  input  A7,
  input  A8,
  input  A9,
  input  A10,
  input  A11,
  input  A12,
  input  A13,
  input  A14,
  input  A15,
  input  A16,
  input  A17,
  input  A18,
  input  A19,
  input  A20,
  input  A21,
  input  A22,
  input  A23,
  input  A24,
  input  A25,
  input  A26,
  input  A27,
  input  A28,
  input  A29,
  input  A30,
  input  A31,
  input  B0,
  input  B1,
  input  B2,
  input  B3,
  input  B4,
  input  B5,
  input  B6,
  input  B7,
  input  B8,
  input  B9,
  input  B10,
  input  B11,
  input  B12,
  input  B13,
  input  B14,
  input  B15,
  input  B16,
  input  B17,
  input  B18,
  input  B19,
  input  B20,
  input  B21,
  input  B22,
  input  B23,
  input  B24,
  input  B25,
  input  B26,
  input  B27,
  input  B28,
  input  B29,
  input  B30,
  input  B31,
  output R0,
  output R1,
  output R2,
  output R3,
  output R4,
  output R5,
  output R6,
  output R7,
  output R8,
  output R9,
  output R10,
  output R11,
  output R12,
  output R13,
  output R14,
  output R15,
  output R16,
  output R17,
  output R18,
  output R19,
  output R20,
  output R21,
  output R22,
  output R23,
  output R24,
  output R25,
  output R26,
  output R27,
  output R28,
  output R29,
  output R30,
  output R31
);

  wire and_1_out, and_2_out, and_3_out, and_4_out, and_5_out, and_6_out, and_7_out, and_8_out, and_9_out,
       and_10_out, and_11_out, and_12_out, and_13_out, and_14_out, and_15_out, and_16_out, and_17_out,
       and_18_out, and_19_out, and_20_out, and_21_out, and_22_out, and_23_out, and_24_out, and_25_out,
       and_26_out, and_27_out, and_28_out, and_29_out, and_30_out, and_31_out, and_32_out, and_33_out,
       and_34_out, and_35_out, and_36_out, and_37_out, and_38_out, and_39_out, and_40_out, and_41_out,
       and_42_out, and_43_out, and_44_out, and_45_out, and_46_out, and_47_out, and_48_out, and_49_out,
       and_50_out, and_51_out, and_52_out, and_53_out, and_54_out, and_55_out, and_56_out, and_57_out,
       and_58_out, and_59_out, and_60_out, and_61_out, and_62_out, and_63_out, and_64_out, not_1_out;

  not not_1 (not_1_out, S);
  and and_1 (and_1_out, A0, not_1_out);
  and and_2 (and_2_out, A1, not_1_out);
  and and_3 (and_3_out, A2, not_1_out);
  and and_4 (and_4_out, A3, not_1_out);
  and and_5 (and_5_out, A4, not_1_out);
  and and_6 (and_6_out, A5, not_1_out);
  and and_7 (and_7_out, A6, not_1_out);
  and and_8 (and_8_out, A7, not_1_out);
  and and_9 (and_9_out, A8, not_1_out);
  and and_10 (and_10_out, A9, not_1_out);
  and and_11 (and_11_out, A10, not_1_out);
  and and_12 (and_12_out, A11, not_1_out);
  and and_13 (and_13_out, A12, not_1_out);
  and and_14 (and_14_out, A13, not_1_out);
  and and_15 (and_15_out, A14, not_1_out);
  and and_16 (and_16_out, A15, not_1_out);
  and and_17 (and_17_out, A16, not_1_out);
  and and_18 (and_18_out, A17, not_1_out);
  and and_19 (and_19_out, A18, not_1_out);
  and and_20 (and_20_out, A19, not_1_out);
  and and_21 (and_21_out, A20, not_1_out);
  and and_22 (and_22_out, A21, not_1_out);
  and and_23 (and_23_out, A22, not_1_out);
  and and_24 (and_24_out, A23, not_1_out);
  and and_25 (and_25_out, A24, not_1_out);
  and and_26 (and_26_out, A25, not_1_out);
  and and_27 (and_27_out, A26, not_1_out);
  and and_28 (and_28_out, A27, not_1_out);
  and and_29 (and_29_out, A28, not_1_out);
  and and_30 (and_30_out, A29, not_1_out);
  and and_31 (and_31_out, A30, not_1_out);
  and and_32 (and_32_out, A31, not_1_out);
  and and_33 (and_33_out, B0, S);
  and and_34 (and_34_out, B1, S);
  and and_35 (and_35_out, B2, S);
  and and_36 (and_36_out, B3, S);
  and and_37 (and_37_out, B4, S);
  and and_38 (and_38_out, B5, S);
  and and_39 (and_39_out, B6, S);
  and and_40 (and_40_out, B7, S);
  and and_41 (and_41_out, B8, S);
  and and_42 (and_42_out, B9, S);
  and and_43 (and_43_out, B10, S);
  and and_44 (and_44_out, B11, S);
  and and_45 (and_45_out, B12, S);
  and and_46 (and_46_out, B13, S);
  and and_47 (and_47_out, B14, S);
  and and_48 (and_48_out, B15, S);
  and and_49 (and_49_out, B16, S);
  and and_50 (and_50_out, B17, S);
  and and_51 (and_51_out, B18, S);
  and and_52 (and_52_out, B19, S);
  and and_53 (and_53_out, B20, S);
  and and_54 (and_54_out, B21, S);
  and and_55 (and_55_out, B22, S);
  and and_56 (and_56_out, B23, S);
  and and_57 (and_57_out, B24, S);
  and and_58 (and_58_out, B25, S);
  and and_59 (and_59_out, B26, S);
  and and_60 (and_60_out, B27, S);
  and and_61 (and_61_out, B28, S);
  and and_62 (and_62_out, B29, S);
  and and_63 (and_63_out, B30, S);
  and and_64 (and_64_out, B31, S);
  or or_1 (R0, and_1_out, and_33_out);
  or or_2 (R1, and_2_out, and_34_out);
  or or_3 (R2, and_3_out, and_35_out);
  or or_4 (R3, and_4_out, and_36_out);
  or or_5 (R4, and_5_out, and_37_out);
  or or_6 (R5, and_6_out, and_38_out);
  or or_7 (R6, and_7_out, and_39_out);
  or or_8 (R7, and_8_out, and_40_out);
  or or_9 (R8, and_9_out, and_41_out);
  or or_10 (R9, and_10_out, and_42_out);
  or or_11 (R10, and_11_out, and_43_out);
  or or_12 (R11, and_12_out, and_44_out);
  or or_13 (R12, and_13_out, and_45_out);
  or or_14 (R13, and_14_out, and_46_out);
  or or_15 (R14, and_15_out, and_47_out);
  or or_16 (R15, and_16_out, and_48_out);
  or or_17 (R16, and_17_out, and_49_out);
  or or_18 (R17, and_18_out, and_50_out);
  or or_19 (R18, and_19_out, and_51_out);
  or or_20 (R19, and_20_out, and_52_out);
  or or_21 (R20, and_21_out, and_53_out);
  or or_22 (R21, and_22_out, and_54_out);
  or or_23 (R22, and_23_out, and_55_out);
  or or_24 (R23, and_24_out, and_56_out);
  or or_25 (R24, and_25_out, and_57_out);
  or or_26 (R25, and_26_out, and_58_out);
  or or_27 (R26, and_27_out, and_59_out);
  or or_28 (R27, and_28_out, and_60_out);
  or or_29 (R28, and_29_out, and_61_out);
  or or_30 (R29, and_30_out, and_62_out);
  or or_31 (R30, and_31_out, and_63_out);
  or or_32 (R31, and_32_out, and_64_out);
endmodule

module OR_32bits (
  input  [31:0] A,
  input  [31:0] B,
  output [31:0] out_3
);

  assign out_3 = A | B;  // OR_Gate OR_GATE, 32 bits wide
endmodule

module AND_32bits (
  input  [31:0] A,
  input  [31:0] B,
  output [31:0] resulted
);

  assign resulted = A & B;  // AND_Gate and_gate, 32 bits wide
endmodule

module XOR_32bits (
  input  [31:0] A,
  input  [31:0] B,
  output [31:0] resulted
);

  assign resulted = A ^ B;  // XOR_Gate xor_gate, 32 bits wide
endmodule

module NOR_gate (
  input  [31:0] A,
  input  [31:0] B,
  output [31:0] resulted
);

  assign resulted = ~(A | B);  // NOR_Gate nor_gate, 32 bits wide
endmodule

module MAIN (
  input  [3:0] AluOp,
  input  [31:0] A,
  input  [31:0] B,
  output out_4,
  output [31:0] RESULTED,
  output out_6
);

  ULA ula_1 (.AluOP(AluOp), .A(A), .B(B), .tudo_zer_cont(out_4), .RESULTED(RESULTED), .tudo_zer_logic(out_6));
endmodule

module MUX_4_1_32bits (
  input  [1:0] S1,
  input  [31:0] A,
  input  [31:0] B,
  input  [31:0] C,
  input  [31:0] D,
  output [31:0] resulted
);

  wire [31:0] mux_2_1_32bit_1_r0, mux_2_1_32bit_2_r0;

  MUX_2_1_32bit mux_2_1_32bit_1 (
    .S(S1[0]), .A0(A[0]), .A1(A[1]), .A2(A[2]), .A3(A[3]), .A4(A[4]), .A5(A[5]), .A6(A[6]), .A7(A[7]),
    .A8(A[8]), .A9(A[9]), .A10(A[10]), .A11(A[11]), .A12(A[12]), .A13(A[13]), .A14(A[14]), .A15(A[15]),
    .A16(A[16]), .A17(A[17]), .A18(A[18]), .A19(A[19]), .A20(A[20]), .A21(A[21]), .A22(A[22]), .A23(A[23]),
    .A24(A[24]), .A25(A[25]), .A26(A[26]), .A27(A[27]), .A28(A[28]), .A29(A[29]), .A30(A[30]), .A31(A[31]),
    .B0(B[0]), .B1(B[1]), .B2(B[2]), .B3(B[3]), .B4(B[4]), .B5(B[5]), .B6(B[6]), .B7(B[7]), .B8(B[8]),
    .B9(B[9]), .B10(B[10]), .B11(B[11]), .B12(B[12]), .B13(B[13]), .B14(B[14]), .B15(B[15]), .B16(B[16]),
    .B17(B[17]), .B18(B[18]), .B19(B[19]), .B20(B[20]), .B21(B[21]), .B22(B[22]), .B23(B[23]), .B24(B[24]),
    .B25(B[25]), .B26(B[26]), .B27(B[27]), .B28(B[28]), .B29(B[29]), .B30(B[30]), .B31(B[31]),
    .R0(mux_2_1_32bit_1_r0[0]), .R1(mux_2_1_32bit_1_r0[1]), .R2(mux_2_1_32bit_1_r0[2]),
    .R3(mux_2_1_32bit_1_r0[3]), .R4(mux_2_1_32bit_1_r0[4]), .R5(mux_2_1_32bit_1_r0[5]),
    .R6(mux_2_1_32bit_1_r0[6]), .R7(mux_2_1_32bit_1_r0[7]), .R8(mux_2_1_32bit_1_r0[8]),
    .R9(mux_2_1_32bit_1_r0[9]), .R10(mux_2_1_32bit_1_r0[10]), .R11(mux_2_1_32bit_1_r0[11]),
    .R12(mux_2_1_32bit_1_r0[12]), .R13(mux_2_1_32bit_1_r0[13]), .R14(mux_2_1_32bit_1_r0[14]),
    .R15(mux_2_1_32bit_1_r0[15]), .R16(mux_2_1_32bit_1_r0[16]), .R17(mux_2_1_32bit_1_r0[17]),
    .R18(mux_2_1_32bit_1_r0[18]), .R19(mux_2_1_32bit_1_r0[19]), .R20(mux_2_1_32bit_1_r0[20]),
    .R21(mux_2_1_32bit_1_r0[21]), .R22(mux_2_1_32bit_1_r0[22]), .R23(mux_2_1_32bit_1_r0[23]),
    .R24(mux_2_1_32bit_1_r0[24]), .R25(mux_2_1_32bit_1_r0[25]), .R26(mux_2_1_32bit_1_r0[26]),
    .R27(mux_2_1_32bit_1_r0[27]), .R28(mux_2_1_32bit_1_r0[28]), .R29(mux_2_1_32bit_1_r0[29]),
    .R30(mux_2_1_32bit_1_r0[30]), .R31(mux_2_1_32bit_1_r0[31]));
  MUX_2_1_32bit mux_2_1_32bit_2 (
    .S(S1[0]), .A0(C[0]), .A1(C[1]), .A2(C[2]), .A3(C[3]), .A4(C[4]), .A5(C[5]), .A6(C[6]), .A7(C[7]),
    .A8(C[8]), .A9(C[9]), .A10(C[10]), .A11(C[11]), .A12(C[12]), .A13(C[13]), .A14(C[14]), .A15(C[15]),
    .A16(C[16]), .A17(C[17]), .A18(C[18]), .A19(C[19]), .A20(C[20]), .A21(C[21]), .A22(C[22]), .A23(C[23]),
    .A24(C[24]), .A25(C[25]), .A26(C[26]), .A27(C[27]), .A28(C[28]), .A29(C[29]), .A30(C[30]), .A31(C[31]),
    .B0(D[0]), .B1(D[1]), .B2(D[2]), .B3(D[3]), .B4(D[4]), .B5(D[5]), .B6(D[6]), .B7(D[7]), .B8(D[8]),
    .B9(D[9]), .B10(D[10]), .B11(D[11]), .B12(D[12]), .B13(D[13]), .B14(D[14]), .B15(D[15]), .B16(D[16]),
    .B17(D[17]), .B18(D[18]), .B19(D[19]), .B20(D[20]), .B21(D[21]), .B22(D[22]), .B23(D[23]), .B24(D[24]),
    .B25(D[25]), .B26(D[26]), .B27(D[27]), .B28(D[28]), .B29(D[29]), .B30(D[30]), .B31(D[31]),
    .R0(mux_2_1_32bit_2_r0[0]), .R1(mux_2_1_32bit_2_r0[1]), .R2(mux_2_1_32bit_2_r0[2]),
    .R3(mux_2_1_32bit_2_r0[3]), .R4(mux_2_1_32bit_2_r0[4]), .R5(mux_2_1_32bit_2_r0[5]),
    .R6(mux_2_1_32bit_2_r0[6]), .R7(mux_2_1_32bit_2_r0[7]), .R8(mux_2_1_32bit_2_r0[8]),
    .R9(mux_2_1_32bit_2_r0[9]), .R10(mux_2_1_32bit_2_r0[10]), .R11(mux_2_1_32bit_2_r0[11]),
    .R12(mux_2_1_32bit_2_r0[12]), .R13(mux_2_1_32bit_2_r0[13]), .R14(mux_2_1_32bit_2_r0[14]),
    .R15(mux_2_1_32bit_2_r0[15]), .R16(mux_2_1_32bit_2_r0[16]), .R17(mux_2_1_32bit_2_r0[17]),
    .R18(mux_2_1_32bit_2_r0[18]), .R19(mux_2_1_32bit_2_r0[19]), .R20(mux_2_1_32bit_2_r0[20]),
    .R21(mux_2_1_32bit_2_r0[21]), .R22(mux_2_1_32bit_2_r0[22]), .R23(mux_2_1_32bit_2_r0[23]),
    .R24(mux_2_1_32bit_2_r0[24]), .R25(mux_2_1_32bit_2_r0[25]), .R26(mux_2_1_32bit_2_r0[26]),
    .R27(mux_2_1_32bit_2_r0[27]), .R28(mux_2_1_32bit_2_r0[28]), .R29(mux_2_1_32bit_2_r0[29]),
    .R30(mux_2_1_32bit_2_r0[30]), .R31(mux_2_1_32bit_2_r0[31]));
  MUX_2_1_32bit mux_2_1_32bit_3 (
    .S(S1[1]), .A0(mux_2_1_32bit_1_r0[0]), .A1(mux_2_1_32bit_1_r0[1]), .A2(mux_2_1_32bit_1_r0[2]),
    .A3(mux_2_1_32bit_1_r0[3]), .A4(mux_2_1_32bit_1_r0[4]), .A5(mux_2_1_32bit_1_r0[5]),
    .A6(mux_2_1_32bit_1_r0[6]), .A7(mux_2_1_32bit_1_r0[7]), .A8(mux_2_1_32bit_1_r0[8]),
    .A9(mux_2_1_32bit_1_r0[9]), .A10(mux_2_1_32bit_1_r0[10]), .A11(mux_2_1_32bit_1_r0[11]),
    .A12(mux_2_1_32bit_1_r0[12]), .A13(mux_2_1_32bit_1_r0[13]), .A14(mux_2_1_32bit_1_r0[14]),
    .A15(mux_2_1_32bit_1_r0[15]), .A16(mux_2_1_32bit_1_r0[16]), .A17(mux_2_1_32bit_1_r0[17]),
    .A18(mux_2_1_32bit_1_r0[18]), .A19(mux_2_1_32bit_1_r0[19]), .A20(mux_2_1_32bit_1_r0[20]),
    .A21(mux_2_1_32bit_1_r0[21]), .A22(mux_2_1_32bit_1_r0[22]), .A23(mux_2_1_32bit_1_r0[23]),
    .A24(mux_2_1_32bit_1_r0[24]), .A25(mux_2_1_32bit_1_r0[25]), .A26(mux_2_1_32bit_1_r0[26]),
    .A27(mux_2_1_32bit_1_r0[27]), .A28(mux_2_1_32bit_1_r0[28]), .A29(mux_2_1_32bit_1_r0[29]),
    .A30(mux_2_1_32bit_1_r0[30]), .A31(mux_2_1_32bit_1_r0[31]), .B0(mux_2_1_32bit_2_r0[0]),
    .B1(mux_2_1_32bit_2_r0[1]), .B2(mux_2_1_32bit_2_r0[2]), .B3(mux_2_1_32bit_2_r0[3]),
    .B4(mux_2_1_32bit_2_r0[4]), .B5(mux_2_1_32bit_2_r0[5]), .B6(mux_2_1_32bit_2_r0[6]),
    .B7(mux_2_1_32bit_2_r0[7]), .B8(mux_2_1_32bit_2_r0[8]), .B9(mux_2_1_32bit_2_r0[9]),
    .B10(mux_2_1_32bit_2_r0[10]), .B11(mux_2_1_32bit_2_r0[11]), .B12(mux_2_1_32bit_2_r0[12]),
    .B13(mux_2_1_32bit_2_r0[13]), .B14(mux_2_1_32bit_2_r0[14]), .B15(mux_2_1_32bit_2_r0[15]),
    .B16(mux_2_1_32bit_2_r0[16]), .B17(mux_2_1_32bit_2_r0[17]), .B18(mux_2_1_32bit_2_r0[18]),
    .B19(mux_2_1_32bit_2_r0[19]), .B20(mux_2_1_32bit_2_r0[20]), .B21(mux_2_1_32bit_2_r0[21]),
    .B22(mux_2_1_32bit_2_r0[22]), .B23(mux_2_1_32bit_2_r0[23]), .B24(mux_2_1_32bit_2_r0[24]),
    .B25(mux_2_1_32bit_2_r0[25]), .B26(mux_2_1_32bit_2_r0[26]), .B27(mux_2_1_32bit_2_r0[27]),
    .B28(mux_2_1_32bit_2_r0[28]), .B29(mux_2_1_32bit_2_r0[29]), .B30(mux_2_1_32bit_2_r0[30]),
    .B31(mux_2_1_32bit_2_r0[31]), .R0(resulted[0]), .R1(resulted[1]), .R2(resulted[2]), .R3(resulted[3]),
    .R4(resulted[4]), .R5(resulted[5]), .R6(resulted[6]), .R7(resulted[7]), .R8(resulted[8]),
    .R9(resulted[9]), .R10(resulted[10]), .R11(resulted[11]), .R12(resulted[12]), .R13(resulted[13]),
    .R14(resulted[14]), .R15(resulted[15]), .R16(resulted[16]), .R17(resulted[17]), .R18(resulted[18]),
    .R19(resulted[19]), .R20(resulted[20]), .R21(resulted[21]), .R22(resulted[22]), .R23(resulted[23]),
    .R24(resulted[24]), .R25(resulted[25]), .R26(resulted[26]), .R27(resulted[27]), .R28(resulted[28]),
    .R29(resulted[29]), .R30(resulted[30]), .R31(resulted[31]));
endmodule

module MUX_7_1_32bits (
  input  [2:0] S1_S2_S3,
  input  [31:0] A_D_D,
  input  [31:0] S_U_B,
  input  [31:0] S_T_L,
  input  [31:0] A_N_D,
  input  [31:0] X_O_R,
  input  [31:0] O_R,
  input  [31:0] N_O_R,
  output [31:0] out_9
);

  wire [31:0] mux_4_1_32bits_1_resulted, mux_4_1_32bits_2_resulted;

  MUX_4_1_32bits mux_4_1_32bits_1 (
    .S1({S1_S2_S3[0], S1_S2_S3[1]}), .A(A_D_D), .B(S_U_B), .D(S_T_L), .resulted(mux_4_1_32bits_1_resulted));  // open: C
  MUX_4_1_32bits mux_4_1_32bits_2 (
    .S1({S1_S2_S3[0], S1_S2_S3[1]}), .A(A_N_D), .B(X_O_R), .C(O_R), .D(N_O_R),
    .resulted(mux_4_1_32bits_2_resulted));
  MUX_2_1_32bit mux_2_1_32bit_1 (
    .S(S1_S2_S3[2]), .A0(mux_4_1_32bits_1_resulted[0]), .A1(mux_4_1_32bits_1_resulted[1]),
    .A2(mux_4_1_32bits_1_resulted[2]), .A3(mux_4_1_32bits_1_resulted[3]), .A4(mux_4_1_32bits_1_resulted[4]),
    .A5(mux_4_1_32bits_1_resulted[5]), .A6(mux_4_1_32bits_1_resulted[6]), .A7(mux_4_1_32bits_1_resulted[7]),
    .A8(mux_4_1_32bits_1_resulted[8]), .A9(mux_4_1_32bits_1_resulted[9]),
    .A10(mux_4_1_32bits_1_resulted[10]), .A11(mux_4_1_32bits_1_resulted[11]),
    .A12(mux_4_1_32bits_1_resulted[12]), .A13(mux_4_1_32bits_1_resulted[13]),
    .A14(mux_4_1_32bits_1_resulted[14]), .A15(mux_4_1_32bits_1_resulted[15]),
    .A16(mux_4_1_32bits_1_resulted[16]), .A17(mux_4_1_32bits_1_resulted[17]),
    .A18(mux_4_1_32bits_1_resulted[18]), .A19(mux_4_1_32bits_1_resulted[19]),
    .A20(mux_4_1_32bits_1_resulted[20]), .A21(mux_4_1_32bits_1_resulted[21]),
    .A22(mux_4_1_32bits_1_resulted[22]), .A23(mux_4_1_32bits_1_resulted[23]),
    .A24(mux_4_1_32bits_1_resulted[24]), .A25(mux_4_1_32bits_1_resulted[25]),
    .A26(mux_4_1_32bits_1_resulted[26]), .A27(mux_4_1_32bits_1_resulted[27]),
    .A28(mux_4_1_32bits_1_resulted[28]), .A29(mux_4_1_32bits_1_resulted[29]),
    .A30(mux_4_1_32bits_1_resulted[30]), .A31(mux_4_1_32bits_1_resulted[31]),
    .B0(mux_4_1_32bits_2_resulted[0]), .B1(mux_4_1_32bits_2_resulted[1]), .B2(mux_4_1_32bits_2_resulted[2]),
    .B3(mux_4_1_32bits_2_resulted[3]), .B4(mux_4_1_32bits_2_resulted[4]), .B5(mux_4_1_32bits_2_resulted[5]),
    .B6(mux_4_1_32bits_2_resulted[6]), .B7(mux_4_1_32bits_2_resulted[7]), .B8(mux_4_1_32bits_2_resulted[8]),
    .B9(mux_4_1_32bits_2_resulted[9]), .B10(mux_4_1_32bits_2_resulted[10]),
    .B11(mux_4_1_32bits_2_resulted[11]), .B12(mux_4_1_32bits_2_resulted[12]),
    .B13(mux_4_1_32bits_2_resulted[13]), .B14(mux_4_1_32bits_2_resulted[14]),
    .B15(mux_4_1_32bits_2_resulted[15]), .B16(mux_4_1_32bits_2_resulted[16]),
    .B17(mux_4_1_32bits_2_resulted[17]), .B18(mux_4_1_32bits_2_resulted[18]),
    .B19(mux_4_1_32bits_2_resulted[19]), .B20(mux_4_1_32bits_2_resulted[20]),
    .B21(mux_4_1_32bits_2_resulted[21]), .B22(mux_4_1_32bits_2_resulted[22]),
    .B23(mux_4_1_32bits_2_resulted[23]), .B24(mux_4_1_32bits_2_resulted[24]),
    .B25(mux_4_1_32bits_2_resulted[25]), .B26(mux_4_1_32bits_2_resulted[26]),
    .B27(mux_4_1_32bits_2_resulted[27]), .B28(mux_4_1_32bits_2_resulted[28]),
    .B29(mux_4_1_32bits_2_resulted[29]), .B30(mux_4_1_32bits_2_resulted[30]),
    .B31(mux_4_1_32bits_2_resulted[31]), .R0(out_9[0]), .R1(out_9[1]), .R2(out_9[2]), .R3(out_9[3]),
    .R4(out_9[4]), .R5(out_9[5]), .R6(out_9[6]), .R7(out_9[7]), .R8(out_9[8]), .R9(out_9[9]),
    .R10(out_9[10]), .R11(out_9[11]), .R12(out_9[12]), .R13(out_9[13]), .R14(out_9[14]), .R15(out_9[15]),
    .R16(out_9[16]), .R17(out_9[17]), .R18(out_9[18]), .R19(out_9[19]), .R20(out_9[20]), .R21(out_9[21]),
    .R22(out_9[22]), .R23(out_9[23]), .R24(out_9[24]), .R25(out_9[25]), .R26(out_9[26]), .R27(out_9[27]),
    .R28(out_9[28]), .R29(out_9[29]), .R30(out_9[30]), .R31(out_9[31]));
endmodule

module BLOCO_LOGICO (
  input  [3:0] S1_S2_S3,
  input  [31:0] A,
  input  [31:0] B,
  output [31:0] RESULTED,
  output tudo_zero
);

  wire [31:0] and_32bits_1_resulted, extersor_1_32_1_out_2, mux_7_1_32bits_1_out_9, nor_gate_1_resulted,
       or_32bits_1_out_3, xor_32bits_1_resulted;

  OR_32bits or_32bits_1 (.A(A), .B(B), .out_3(or_32bits_1_out_3));
  AND_32bits and_32bits_1 (.A(A), .B(B), .resulted(and_32bits_1_resulted));
  XOR_32bits xor_32bits_1 (.A(A), .B(B), .resulted(xor_32bits_1_resulted));
  NOR_gate nor_gate_1 (.A(A), .B(B), .resulted(nor_gate_1_resulted));
  EXTERSOR_1_32 extersor_1_32_1 (.in_1(S1_S2_S3[3]), .out_2(extersor_1_32_1_out_2));
  comparador comparador_1 (
    .A(and_32bits_1_resulted), .B(xor_32bits_1_resulted), .C(xor_32bits_1_resulted), .D(nor_gate_1_resulted),
    .tudo_zero(tudo_zero));
  MUX_7_1_32bits mux_7_1_32bits_1 (
    .S1_S2_S3(S1_S2_S3[2:0]), .A_N_D(and_32bits_1_resulted), .X_O_R(xor_32bits_1_resulted),
    .O_R(or_32bits_1_out_3), .N_O_R(nor_gate_1_resulted), .out_9(mux_7_1_32bits_1_out_9));  // open: A_D_D, S_U_B, S_T_L
  assign RESULTED = extersor_1_32_1_out_2 & mux_7_1_32bits_1_out_9;  // AND_Gate and_1, 32 bits wide

  // Notes on the sheet:
  //   1101
  //   1100
  //   1110
  //   1111
endmodule

module EXTERSOR_1_32 (
  input  in_1,
  output [31:0] out_2
);


  assign out_2 = {32{in_1}};
endmodule

module BLOBO_CONT (
  input  [3:0] AluOp,
  input  [31:0] A,
  input  [31:0] B,
  output [31:0] RESULTED,
  output tudo_zero
);

  wire [31:0] add_resumido_32bits_1_out_3, extersor_1_32_1_out_2, extersor_1_32_2_out_2,
       mux_7_1_32bits_1_out_9, stl_1_out_3, sub_resumido_32bits_1_out_3;

  EXTERSOR_1_32 extersor_1_32_1 (.in_1(AluOp[3]), .out_2(extersor_1_32_1_out_2));
  add_resumido_32bits add_resumido_32bits_1 (.A(A), .B(B), .out_3(add_resumido_32bits_1_out_3));
  sub_resumido_32bits sub_resumido_32bits_1 (.A(A), .B(B), .out_3(sub_resumido_32bits_1_out_3));
  stl stl_1 (.A(A), .B(B), .out_3(stl_1_out_3));
  EXTERSOR_1_32 extersor_1_32_2 (.in_1(1'b0), .out_2(extersor_1_32_2_out_2));
  assign RESULTED = ~extersor_1_32_1_out_2 & mux_7_1_32bits_1_out_9;  // AND_Gate and_1, 32 bits wide
  MUX_7_1_32bits mux_7_1_32bits_1 (
    .S1_S2_S3(AluOp[2:0]), .A_D_D(add_resumido_32bits_1_out_3), .S_U_B(sub_resumido_32bits_1_out_3),
    .S_T_L(stl_1_out_3), .out_9(mux_7_1_32bits_1_out_9));  // open: A_N_D, X_O_R, O_R, N_O_R
  comparador comparador_1 (
    .A(add_resumido_32bits_1_out_3), .B(add_resumido_32bits_1_out_3), .C(stl_1_out_3),
    .D(extersor_1_32_2_out_2), .tudo_zero(tudo_zero));

  // Notes on the sheet:
  //   0000
  //   0010
  //   0011
endmodule
